# Fritzing sketch esquema (saved by Fritzing 0.9.3b)
breadboards: 1

parts:
  Raspberry_Pi_1 = Raspberry Pi 3 [part_number=RPI-3-V1.2]
  LED1 = LED - 5mm [color="Green (555nm)" package="5 mm [THT]"]
  LED2 = smd LED [color="Blue (470nm)" package="0603 [SMD]"]

nets:
  N1: Raspberry_Pi_1.GIPO17, LED1.anode
  N2: Raspberry_Pi_1.GND, LED1.cathode, LED2.cathode
